# Fritzing sketch RPI Roobma Conector (saved by Fritzing 0.9.0b)
circuit board: 8.46667cm x 5.64444cm

parts:
  R3 = Resistor [tolerance=±5% resistance=10k package=THT]
  R4 = Resistor [tolerance=±5% resistance=10k package=THT]
  Q5 = MOSFET-NCHANNEL [package=to-92]
  Q6 = MOSFET-NCHANNEL [package=to-92]
  Q8 = MOSFET-NCHANNEL [package=to-92]
  U1 = Voltage Regulator - 5V [package="TO220 [THT]"]
  Roomba = female pin header, 5 pins [form="♀ (female)"]
  RPI = female pin header, 6 pins [form="♀ (female)"]
  I2C = female pin header, 4 pins [form="♀ (female)"]
  Q7 = MOSFET-NCHANNEL [package=to-92]
  R5 = Resistor [tolerance=±5% resistance=10k package=THT]
  R6 = Resistor [tolerance=±5% resistance=10k package=THT]
  RPI_USB = female pin header, 4 pins [form="♀ (female)"]
  LED1 = LED - 5mm [color="Green (555nm)" package="5 mm [THT]"]
  R7 = Resistor [tolerance=±5% resistance=220 package=THT]

nets:
  N1: R3.Pin_0, R4.Pin_0, Q5.G, Q6.G, Q8.G, RPI.pin1, Q7.G
  N2: R3.Pin_1, Q8.D, RPI.pin5
  N3: R4.Pin_1, Q6.D, RPI.pin4
  N4: Q5.D, RPI.pin2
  N5: Q5.S, Roomba.pin2
  N6: Q6.S, I2C.pin3, R5.Pin_0
  N7: Q8.S, I2C.pin2, R6.Pin_0
  N8: U1.input_voltage, Roomba.pin5
  N9: U1.GND, Roomba.pin4, RPI.pin6, I2C.pin1, RPI_USB.pin1, R7.Pin_0
  N10: U1.output_voltage, I2C.pin4, R5.Pin_1, R6.Pin_1, RPI_USB.pin4, LED1.cathode
  N11: Roomba.pin3, Q7.S
  N12: RPI.pin3, Q7.D
  N13: LED1.anode, R7.Pin_1

notes:
  +3V
  SDA
  RX
  TX
  SCL
  GND
  +14V
  Baud
  +5V
